// Logisim project schematic.circ as structural Verilog
module main (
);

  wire AIA, AIB, ALO, and_1_out, CF, CLK, ctrl_1_iric, ctrl_1_jnz, ctrl_1_pcl, MAI, MR, MSL, MW, PCE, PCL,
       PCO, RGI, RGO, SF, socpio_1_p1, SWP, SWP_STATE, ZF;
  wire [2:0] RSEL;
  wire [3:0] ALF;
  wire [15:0] alu16_1_o, prgm_counter_1_dout;

  // Probe on RSEL
  Clock clock_1 (.out(CLK));
  prgm_counter prgm_counter_1 (.PCE(PCE), .PCL(PCL), .DIN(alu16_1_o), .CLK(CLK), .DOUT(prgm_counter_1_dout));
  alu16 alu16_1 (
    .ALUOUT(ALO), .FUNC(ALF), .INB(AIB), .B(alu16_1_o), .CLK(CLK), .INA(AIA), .A(alu16_1_o), .O(alu16_1_o),
    .ZF(ZF), .SF(SF), .Cout(CF));
  registers registers_1 (
    .nWE(RGI), .nOE(RGO), .SEL(RSEL), .DIN(alu16_1_o), .GPU_READY(ZF), .ZF(CF), .CF(SF), .SF(CLK),
    .DOUT(alu16_1_o));  // open: in_5, CLK
  J_K_Flip_Flop j_k_ff_1 (.J(SWP), .K(SWP), .clk(CLK), .Q(SWP_STATE));  // open: Qn, preset, reset
  buffer16 buffer16_1 (.A(prgm_counter_1_dout), .OE(PCO), .B(alu16_1_o));
  // Probe on alu16_1_o
  // mem mem_1: pin names not known; wires that end beside it: SWP_STATE, alu16_1_o, MR, MW, MSL, CLK, MAI, alu16_1_o, alu16_1_o
  ctrl ctrl_1 (
    .IRI(ctrl_1_iric), .CLK(CLK), .IRDI(alu16_1_o), .MW(MW), .MR(MR), .MSL(MSL), .MAI(MAI),
    .IRIC(ctrl_1_iric), .RSEL(RSEL), .RGI(RGI), .RGO(RGO), .INA(AIA), .INB(AIB), .ALF(ALF), .ALO(ALO),
    .PCE(PCE), .PCL(ctrl_1_pcl), .PCO(PCO), .SWP(SWP), .JNZ(ctrl_1_jnz));  // open: HLT, MCR
  Multiplexer multiplexer_1 (.in0(ctrl_1_pcl), .in1(and_1_out), .out(PCL), .sel(ctrl_1_jnz));
  and and_1 (and_1_out, ZF, ctrl_1_jnz);
  // SocPio #(.SocBusSelection('h000001979CA9DADD342a5c2f), .width(16)) socpio_1: pin names not known; wires that end beside it: socpio_1_p1, socpio_1_p1
  // PortIO #(.direction("onlyOutput"), .number(16)) portio_1: pin names not known
  // SocVga #(.DisplayMode("1024x768"), .SocBusSelection('h000001979CA9DADD342a5c2f)) socvga_1: pin names not known
  // SocBus #(.SocBusIdentifier('h000001979CA9DADD342a5c2f)) socbus_1: pin names not known
endmodule

module alu4 (
  input  [3:0] INA,
  input  [3:0] INB,
  input  Cin,
  input  M,
  input  [3:0] S,
  output y,
  output Co,
  output x,
  output eq,
  output [3:0] F
);

  // _74181 74181_1: pin names not known; wires that end beside it: INB[0], INA[0], S[3], S[2], S[1], S[0], Cin, M, F[0], F[1], F[2], INA[1], INB[1], INA[2], INB[2], INA[3], INB[3], y, Co, x, eq, F[3]

  // Other names for the same wires on the sheet: A0 = INA[0]; A1 = INA[1]; A2 = INA[2]; A3 = INA[3]; B0 = INB[0];
  //   B1 = INB[1]; B2 = INB[2]; B3 = INB[3]
endmodule

module alu16 (
  input  INB,
  input  [15:0] B,
  input  CLK,
  input  INA,
  input  [15:0] A,
  input  [3:0] FUNC,
  input  ALUOUT,
  output Cout,
  output [15:0] O,
  output ZF,
  output SF
);

  wire alu4_4_co, Cn, Cnx, Cny, Cnz, M, not_2_out, or_1_out, X0, X1, X2, X3, Y0, Y1, Y2, Y3;
  wire [3:0] alu4_1_f, alu4_2_f, alu4_3_f, alu4_4_f, S;
  wire [7:6] rom_1_data;
  wire [15:0] reg16_1_dout, reg16_2_dout;

  ROM #(.addrWidth(4)) rom_1 (.addr(FUNC), .data({rom_1_data, Cn, M, S}));
  reg16 reg16_1 (.DIN(B), .CLK(CLK), .WE(INB), .OE(1'b0), .DOUT(reg16_1_dout));
  reg16 reg16_2 (.DIN(A), .CLK(CLK), .WE(INA), .OE(1'b0), .DOUT(reg16_2_dout));
  alu4 alu4_1 (
    .INA(reg16_2_dout[3:0]), .INB(reg16_1_dout[3:0]), .Cin(Cn), .M(M), .S(S), .y(Y0), .x(X0), .F(alu4_1_f));  // open: Co, eq
  alu4 alu4_2 (
    .INA(reg16_2_dout[7:4]), .INB(reg16_1_dout[7:4]), .Cin(Cnx), .M(M), .S(S), .y(Y1), .x(X1), .F(alu4_2_f));  // open: Co, eq
  alu4 alu4_3 (
    .INA(reg16_2_dout[11:8]), .INB(reg16_1_dout[11:8]), .Cin(Cny), .M(M), .S(S), .y(Y2), .x(X2), .F(alu4_3_f));  // open: Co, eq
  alu4 alu4_4 (
    .INA(reg16_2_dout[15:12]), .INB(reg16_1_dout[15:12]), .Cin(Cnz), .M(M), .S(S), .y(Y3), .Co(alu4_4_co),
    .x(X3), .F(alu4_4_f));  // open: eq
  not not_1 (Cout, alu4_4_co);
  or or_1 (or_1_out, alu4_4_f[3], alu4_4_f[2], alu4_4_f[1], alu4_4_f[0], alu4_3_f[3], alu4_3_f[2], alu4_3_f[1], alu4_3_f[0], alu4_2_f[3], alu4_2_f[2], alu4_2_f[1], alu4_2_f[0], alu4_1_f[3], alu4_1_f[2], alu4_1_f[1], alu4_1_f[0]);
  not not_2 (not_2_out, or_1_out);
  _74182 u_74182_1 (
    .pin1(Y1), .pin2(X1), .pin3(Y0), .pin4(X0), .pin5(Y3), .pin6(X3), .pin15(X2), .pin14(Y2), .pin13(Cn),
    .pin12(Cnx), .pin11(Cny), .pin9(Cnz));  // open: pin7, pin10
  buffer16 buffer16_1 (.A({alu4_4_f, alu4_3_f, alu4_2_f, alu4_1_f}), .OE(ALUOUT), .B(O));
  D_Flip_Flop #(.trigger("low")) d_ff_1 (.D(not_2_out), .clk(ALUOUT), .Q(ZF));  // open: Qn, preset, reset
  D_Flip_Flop #(.trigger("low")) d_ff_2 (.D(alu4_4_f[3]), .clk(ALUOUT), .Q(SF));  // open: Qn, preset, reset

  // Notes on the sheet:
  //   contents of rom_1 (hex, n*v repeats v):
  //   33 30 29 23 36 3e 31 34 0 2f 2c 20 6 3c 3b
endmodule

module mem (
  input  MAL,
  input  CLK,
  input  [15:0] CPU_ADDR,
  input  GR,
  input  [15:0] GADDR,
  input  [15:0] CDATAIN,
  input  SEL,
  input  CRE,
  input  CW,
  input  RSE,
  output [15:0] GDATAOUT0,
  output [15:0] CDATAOUT
);

  wire not_1_out, not_2_out, or_1_out, or_2_out, or_3_out, or_4_out, or_5_out;
  wire [15:0] reg16_1_dout, rom_1_data;

  reg16 reg16_1 (.DIN(CPU_ADDR), .CLK(CLK), .WE(MAL), .OE(1'b0), .DOUT(reg16_1_dout));
  or or_1 (or_1_out, CRE, not_1_out);
  not not_1 (not_1_out, RSE);
  or or_2 (or_2_out, not_2_out, RSE, CRE);
  or or_3 (or_3_out, not_2_out, RSE, CW);
  not not_2 (not_2_out, reg16_1_dout[15]);
  or or_4 (or_4_out, reg16_1_dout[15], RSE, CW);
  or or_5 (or_5_out, reg16_1_dout[15], RSE, CRE);
  ROM #(.addrWidth(16), .dataWidth(16)) rom_1 (.addr(reg16_1_dout), .data(rom_1_data));
  IS61 is61_1 (.ADDR(reg16_1_dout[14:0]), .WE(or_4_out), .OE(or_5_out), .DIN(CDATAIN), .DOUT(CDATAOUT));
  double_buffer double_buffer_1 (
    .ADDR0(reg16_1_dout), .ADDR1(GADDR), .R1(GR), .R0(or_2_out), .W1(1'b0), .W0(or_3_out), .SEL(SEL),
    .DATAIN0(CDATAIN), .DATAOUT0(CDATAOUT), .DATAOUT1(GDATAOUT0));  // open: DATAIN1
  buffer16 buffer16_1 (.A(rom_1_data), .OE(or_1_out), .B(CDATAOUT));

  // Notes on the sheet:
  //   CW: pull=up
  //   contents of rom_1 (hex, n*v repeats v):
  //   c20 1 c60 1 cb8 b9 c78 c3a c08 0 2000 4
endmodule

module IS61 (
  input  [15:0] DIN,
  input  [14:0] ADDR,
  input  WE,
  input  OE,
  output [15:0] DOUT
);

  wire and_1_out, not_1_out, not_2_out;
  wire [15:0] controlled_buffer_1_out;

  not not_1 (not_1_out, OE);
  RAM #(.addrWidth(15), .dataWidth(16), .databus("bidir"), .trigger("high")) ram_1 (
    .addr(ADDR), .we(not_2_out), .oe(and_1_out));  // open: clk, data
  not not_2 (not_2_out, WE);
  and and_1 (and_1_out, WE, not_1_out);
  assign controlled_buffer_1_out = not_2_out ? DIN : 16'bz;  // Controlled_Buffer controlled_buffer_1
  assign DOUT = and_1_out ? controlled_buffer_1_out : 16'bz;  // Controlled_Buffer controlled_buffer_2

  // Notes on the sheet:
  //   WE: pull=up
  //   OE: pull=up
endmodule

module dbel (
  input  SEL,
  input  [15:0] ADDR0,
  input  [15:0] ADDR1,
  input  R1,
  input  R0,
  input  W1,
  input  W0,
  input  [15:0] DATAIN0,
  input  [15:0] DATAIN1,
  output [15:0] DATAOUT0,
  output [15:0] DATAOUT1
);

  wire and_1_out, and_2_out, E0, E1, not_1_out, not_2_out, not_3_out, not_4_out, R, W;
  wire [15:0] ADDR, bidirectional_buffer16_2_b_out, controlled_buffer_1_out, is61_1_dout;

  not not_1 (not_1_out, SEL);
  buffer16 buffer16_1 (.A(ADDR0), .OE(SEL), .B(ADDR));
  buffer16 buffer16_2 (.A(ADDR1), .OE(not_1_out), .B(ADDR));
  IS61 is61_1 (.ADDR(ADDR[14:0]), .WE(W), .OE(R), .DIN(is61_1_dout), .DOUT(is61_1_dout));
  Multiplexer multiplexer_1 (.in0(W0), .in1(W1), .out(W), .sel(SEL));
  Multiplexer multiplexer_2 (.in0(R0), .in1(R1), .out(R), .sel(SEL));
  assign controlled_buffer_1_out = not_2_out ? DATAIN0 : 16'bz;  // Controlled_Buffer controlled_buffer_1
  bidirectional_buffer16 bidirectional_buffer16_1 (
    .OE(E0), .DIR(W0), .A_IN(is61_1_dout), .B_IN(controlled_buffer_1_out), .B_OUT(controlled_buffer_1_out),
    .A_OUT(is61_1_dout));
  not not_2 (not_2_out, W0);
  bidirectional_buffer16 bidirectional_buffer16_2 (
    .OE(E1), .DIR(W1), .A_IN(is61_1_dout), .B_IN(bidirectional_buffer16_2_b_out),
    .B_OUT(bidirectional_buffer16_2_b_out), .A_OUT(is61_1_dout));
  and and_1 (and_1_out, R1, W1);
  and and_2 (and_2_out, R0, W0);
  assign DATAOUT0 = W0 ? controlled_buffer_1_out : 16'bz;  // Controlled_Buffer controlled_buffer_2
  assign bidirectional_buffer16_2_b_out = not_3_out ? DATAIN1 : 16'bz;  // Controlled_Buffer controlled_buffer_3
  assign DATAOUT1 = W1 ? bidirectional_buffer16_2_b_out : 16'bz;  // Controlled_Buffer controlled_buffer_4
  not not_3 (not_3_out, W1);
  not not_4 (not_4_out, SEL);
  or or_1 (E0, SEL, and_2_out);
  or or_2 (E1, and_1_out, not_4_out);
endmodule

module buffer16 (
  input  [15:0] A,
  input  OE,
  output [15:0] B
);

  wire not_1_out;

  not not_1 (not_1_out, OE);
  assign B = not_1_out ? A : 16'bz;  // Controlled_Buffer controlled_buffer_1

  // Notes on the sheet:
  //   OE: pull=up
endmodule

module buffer15 (
  input  [14:0] A,
  input  OE,
  output [14:0] B
);

  wire not_1_out;

  assign B = not_1_out ? A : 15'bz;  // Controlled_Buffer controlled_buffer_1
  not not_1 (not_1_out, OE);
endmodule

module double_buffer (
  input  [15:0] DATAIN1,
  input  [15:0] DATAIN0,
  input  SEL,
  input  [15:0] ADDR0,
  input  [15:0] ADDR1,
  input  R1,
  input  R0,
  input  W1,
  input  W0,
  output [15:0] DATAOUT0,
  output [15:0] DATAOUT1
);

  wire not_1_out;

  not not_1 (not_1_out, SEL);
  dbel dbel_1 (
    .SEL(SEL), .ADDR0(ADDR0), .ADDR1(ADDR1), .R1(R1), .R0(R0), .W1(W1), .W0(W0), .DATAIN0(DATAIN0),
    .DATAIN1(DATAIN1), .DATAOUT0(DATAOUT0), .DATAOUT1(DATAOUT1));
  dbel dbel_2 (
    .SEL(not_1_out), .ADDR0(ADDR0), .ADDR1(ADDR1), .R1(R1), .R0(R0), .W1(W1), .W0(W0), .DATAIN0(DATAIN0),
    .DATAIN1(DATAIN1), .DATAOUT0(DATAOUT0), .DATAOUT1(DATAOUT1));
endmodule

module bidirectional_buffer16 (
  input  DIR,
  input  OE,
  input  [15:0] A_IN,
  input  [15:0] B_IN,
  output [15:0] B_OUT,
  output [15:0] A_OUT
);

  wire and_1_out, and_2_out, not_1_out, not_2_out;

  not not_1 (not_1_out, OE);
  not not_2 (not_2_out, DIR);
  and and_1 (and_1_out, not_2_out, not_1_out);
  assign A_OUT = and_1_out ? B_IN : 16'bz;  // Controlled_Buffer controlled_buffer_1
  and and_2 (and_2_out, DIR, not_1_out);
  assign B_OUT = and_2_out ? A_IN : 16'bz;  // Controlled_Buffer controlled_buffer_2
endmodule

module SST39SF010A (
  input  [16:0] ADDR,
  input  OE,
  output [7:0] DOUT
);

  wire not_1_out;
  wire [7:0] rom_1_data;

  ROM #(.addrWidth(17)) rom_1 (.addr(ADDR), .data(rom_1_data));
  assign DOUT = not_1_out ? rom_1_data : 8'bz;  // Controlled_Buffer controlled_buffer_1
  not not_1 (not_1_out, OE);

  // Notes on the sheet:
  //   contents of rom_1 (hex, n*v repeats v):
  //   4
endmodule

module reg16 (
  input  WE,
  input  [15:0] DIN,
  input  CLK,
  input  OE,
  output [15:0] DOUT
);

  wire not_1_out, not_2_out;
  wire [15:0] register_1_q;

  Register #(.width(16)) register_1 (.D(DIN), .en(not_1_out), .clk(CLK), .Q(register_1_q));  // open: clr
  not not_1 (not_1_out, WE);
  assign DOUT = not_2_out ? register_1_q : 16'bz;  // Controlled_Buffer controlled_buffer_1
  not not_2 (not_2_out, OE);
endmodule

module prgm_counter (
  input  PCL,
  input  PCE,
  input  CLK,
  input  [15:0] DIN,
  output [15:0] DOUT
);

  wire not_1_out;

  not not_1 (not_1_out, PCL);
  Counter #(.max('hffff), .width(16)) counter_1 (
    .load(not_1_out), .up(1'b1), .count(PCE), .clk(CLK), .D(DIN), .Q(DOUT));  // open: clr, carry
endmodule

module ctrl (
  input  IRI,
  input  [15:0] IRDI,
  input  CLK,
  output MW,
  output MR,
  output MSL,
  output MAI,
  output IRIC,
  output [2:0] RSEL,
  output RGI,
  output RGO,
  output INA,
  output INB,
  output [3:0] ALF,
  output ALO,
  output PCE,
  output PCL,
  output PCO,
  output HLT,
  output MCR,
  output SWP,
  output JNZ
);

  wire n74161_1_pin2, n74161_1_pin7, n74161_1_pin10;
  wire [3:0] n74161_1_pin14;
  wire [15:0] reg16_1_dout;

  _74161 u_74161_1 (
    .pin1(MCR), .pin2(n74161_1_pin2), .pin7(n74161_1_pin7), .pin14(n74161_1_pin14[0]),
    .pin13(n74161_1_pin14[1]), .pin12(n74161_1_pin14[2]), .pin11(n74161_1_pin14[3]), .pin10(n74161_1_pin10),
    .pin9(n74161_1_pin10));  // open: pin3, pin4, pin5, pin6, pin15
  not not_1 (n74161_1_pin2, CLK);
  reg16 reg16_1 (.DIN(IRDI), .CLK(CLK), .WE(IRI), .OE(1'b0), .DOUT(reg16_1_dout));
  // Probe on reg16_1_dout[13:0]
  // Probe on {reg16_1_dout[13:0], n74161_1_pin14}
  ROM #(.addrWidth(18), .dataWidth(24)) rom_1 (
    .addr({reg16_1_dout[13:0], n74161_1_pin14}),
    .data({JNZ, SWP, MCR, HLT, PCO, PCL, PCE, ALO, ALF, INB, INA, RGO, RGI, RSEL, IRIC, MAI, MSL, MR, MW}));
  // also tied to VCC on the sheet: {n74161_1_pin10, n74161_1_pin7}

  // Notes on the sheet:
  //   contents of rom_1 (hex, n*v repeats v):
  //   250f13 2f0f0d 510*2d0f1b 250f13 2f0f0d 250f13 2f0b1d 2d051b 2c2e1b d0f1b 313*2d0f1b 250f13 2f0f0d
  //   250f13 2f071d 2d09d3 2cff1a 2c8edb d0f1b 8*2d0f1b 250f13 2f0f0d 250f13 2f0f15 2d0719 2d09d3 2cff1a
  //   2c8edb d0f1b 39*2d0f1b 250f13 2f0f0d 2d091b 2d051b 2c2e1b d0f1b 10*2d0f1b 250f13 2f0f0d 2d093b
  //   2d051b 2c2e1b d0f1b 10*2d0f1b 250f13 2f0f0d 2d095b 2d051b 2c2e1b d0f1b 10*2d0f1b 250f13 2f0f0d
  //   2d097b 2d051b 2c2e1b d0f1b 10*2d0f1b 250f13 2f0f0d 2d099b 2d051b 2c2e1b d0f1b 10*2d0f1b 250f13
  //   2f0f0d 2d09bb 2d051b 2c2e1b d0f1b 10*2d0f1b 250f13 2f0f0d 2d09db 2d051b 2c2e1b d0f1b 10*2d0f1b
  //   250f13 2f0f0d 2d09fb 2d051b 2c2e1b d0f1b 522*2d0f1b 250f13 2f0f0d 250f13 2f0b1d 2d053b 2c2e3b d0f1b
  //   377*2d0f1b 250f13 2f0f0d 2d091b 2d053b 2c2e3b d0f1b 10*2d0f1b 250f13 2f0f0d 2d093b 2d053b 2c2e3b
  //   d0f1b 10*2d0f1b 250f13 2f0f0d 2d095b 2d053b 2c2e3b d0f1b 10*2d0f1b 250f13 2f0f0d 2d097b 2d053b
  //   2c2e3b d0f1b 10*2d0f1b 250f13 2f0f0d 2d099b 2d053b 2c2e3b d0f1b 10*2d0f1b 250f13 2f0f0d 2d09bb
  //   2d053b 2c2e3b d0f1b 10*2d0f1b 250f13 2f0f0d 2d09db 2d053b 2c2e3b d0f1b 10*2d0f1b 250f13 2f0f0d
  //   2d09fb 2d053b 2c2e3b d0f1b 522*2d0f1b 250f13 2f0f0d 250f13 2f0b1d 2d055b 2c2e5b d0f1b 377*2d0f1b
  //   250f13 2f0f0d 2d091b 2d055b 2c2e5b d0f1b 10*2d0f1b 250f13 2f0f0d 2d093b 2d055b 2c2e5b d0f1b
  //   10*2d0f1b 250f13 2f0f0d 2d095b 2d055b 2c2e5b d0f1b 10*2d0f1b 250f13 2f0f0d 2d097b 2d055b 2c2e5b
  //   d0f1b 10*2d0f1b 250f13 2f0f0d 2d099b 2d055b 2c2e5b d0f1b 10*2d0f1b 250f13 2f0f0d 2d09bb 2d055b
  //   2c2e5b d0f1b 10*2d0f1b 250f13 2f0f0d 2d09db 2d055b 2c2e5b d0f1b 10*2d0f1b 250f13 2f0f0d 2d09fb
  //   2d055b 2c2e5b d0f1b 522*2d0f1b 250f13 2f0f0d 250f13 2f0b1d 2d057b 2c2e7b d0f1b 377*2d0f1b 250f13
  //   2f0f0d 2d091b 2d057b 2c2e7b d0f1b 10*2d0f1b 250f13 2f0f0d 2d093b 2d057b 2c2e7b d0f1b 10*2d0f1b
  //   250f13 2f0f0d 2d095b 2d057b 2c2e7b d0f1b 10*2d0f1b 250f13 2f0f0d 2d097b 2d057b 2c2e7b d0f1b
  //   10*2d0f1b 250f13 2f0f0d 2d099b 2d057b 2c2e7b d0f1b 10*2d0f1b 250f13 2f0f0d 2d09bb 2d057b 2c2e7b
  //   d0f1b 10*2d0f1b 250f13 2f0f0d 2d09db 2d057b 2c2e7b d0f1b 10*2d0f1b 250f13 2f0f0d 2d09fb 2d057b
  //   2c2e7b d0f1b 522*2d0f1b 250f13 2f0f0d 250f13 2f0b1d 2d059b 2c2e9b d0f1b 377*2d0f1b 250f13 2f0f0d
  //   2d091b 2d059b 2c2e9b d0f1b 10*2d0f1b 250f13 2f0f0d 2d093b 2d059b 2c2e9b d0f1b 10*2d0f1b 250f13
  //   2f0f0d 2d095b 2d059b 2c2e9b d0f1b 10*2d0f1b 250f13 2f0f0d 2d097b 2d059b 2c2e9b d0f1b 10*2d0f1b
  //   250f13 2f0f0d 2d099b 2d059b 2c2e9b d0f1b 10*2d0f1b 250f13 2f0f0d 2d09bb 2d059b 2c2e9b d0f1b
  //   10*2d0f1b 250f13 2f0f0d 2d09db 2d059b 2c2e9b d0f1b 10*2d0f1b 250f13 2f0f0d 2d09fb 2d059b 2c2e9b
  //   d0f1b 522*2d0f1b 250f13 2f0f0d 250f13 2f0b1d 2d05bb 2c2ebb d0f1b 377*2d0f1b 250f13 2f0f0d 2d091b
  //   2d05bb 2c2ebb d0f1b 10*2d0f1b 250f13 2f0f0d 2d093b 2d05bb 2c2ebb d0f1b 10*2d0f1b 250f13 2f0f0d
  //   2d095b 2d05bb 2c2ebb d0f1b 10*2d0f1b 250f13 2f0f0d 2d097b 2d05bb 2c2ebb d0f1b 10*2d0f1b 250f13
  //   2f0f0d 2d099b 2d05bb 2c2ebb d0f1b 10*2d0f1b 250f13 2f0f0d 2d09bb 2d05bb 2c2ebb d0f1b 10*2d0f1b
  //   250f13 2f0f0d 2d09db 2d05bb 2c2ebb d0f1b 10*2d0f1b 250f13 2f0f0d 2d09fb 2d05bb 2c2ebb d0f1b
  //   522*2d0f1b 250f13 2f0f0d 250f13 2f0b1d 2d05db 2c2edb d0f1b 249*2d0f1b 250f13 2f0f0d 2d0d13 2d0719
  //   2d09d3 2cff1a 2c8edb d0f1b 8*2d0f1b 250f13 2f0f0d 2d0d33 2d0719 2d09d3 2cff1a 2c8edb d0f1b 8*2d0f1b
  //   250f13 2f0f0d 2d0d53 2d0719 2d09d3 2cff1a 2c8edb d0f1b 8*2d0f1b 250f13 2f0f0d 2d0d73 2d0719 2d09d3
  //   2cff1a 2c8edb d0f1b 8*2d0f1b 250f13 2f0f0d 2d0d93 2d0719 2d09d3 2cff1a 2c8edb d0f1b 8*2d0f1b 250f13
  //   2f0f0d 2d0db3 2d0719 2d09d3 2cff1a 2c8edb d0f1b 8*2d0f1b 250f13 2f0f0d 2d0dd3 2d0719 2d09d3 2cff1a
  //   2c8edb d0f1b 8*2d0f1b 250f13 2f0f0d 2d0df3 2d0719 2d09d3 2cff1a 2c8edb d0f1b 8*2d0f1b 250f13 2f0f0d
  //   2d091b 2d05db 2c2edb d0f1b 10*2d0f1b 250f13 2f0f0d 2d093b 2d05db 2c2edb d0f1b 10*2d0f1b 250f13
  //   2f0f0d 2d095b 2d05db 2c2edb d0f1b 10*2d0f1b 250f13 2f0f0d 2d097b 2d05db 2c2edb d0f1b 10*2d0f1b
  //   250f13 2f0f0d 2d099b 2d05db 2c2edb d0f1b 10*2d0f1b 250f13 2f0f0d 2d09bb 2d05db 2c2edb d0f1b
  //   10*2d0f1b 250f13 2f0f0d 2d09db 2d05db 2c2edb d0f1b 10*2d0f1b 250f13 2f0f0d 2d09fb 2d05db 2c2edb
  //   d0f1b 266*2d0f1b 250f13 2f0f0d 2d09d3 2d0719 2d0d13 2dff1a d0f1b 9*2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
endmodule

module reg4x16 (
  input  nOE,
  input  nWE,
  input  nSEL,
  input  CLK,
  input  [1:0] ADDR,
  input  [15:0] DIN,
  output [15:0] DOUT
);

  wire or_1_out, or_2_out;
  wire [1:0] n74670_1_pin5;

  or or_1 (or_1_out, nOE, nSEL);
  or or_2 (or_2_out, nWE, nSEL);
  Logi74670 logi74670_1 (.nWE(or_2_out), .CLK(CLK), .ADDR(ADDR), .DIN(DIN[3:0]), .nOE(or_1_out), .DOUT(DOUT[3:0]));
  Logi74670 logi74670_2 (.nWE(or_2_out), .CLK(CLK), .ADDR(ADDR), .DIN(DIN[7:4]), .nOE(or_1_out), .DOUT(DOUT[7:4]));
  Logi74670 logi74670_3 (.nWE(or_2_out), .CLK(CLK), .ADDR(ADDR), .DIN(DIN[11:8]), .nOE(or_1_out), .DOUT(DOUT[11:8]));
  Logi74670 logi74670_4 (.nWE(or_2_out), .CLK(CLK), .ADDR(ADDR), .DIN(DIN[15:12]), .nOE(or_1_out), .DOUT(DOUT[15:12]));
  _74670 u_74670_1 (
    .pin4(n74670_1_pin5[1]), .pin5(n74670_1_pin5[0]), .pin14(n74670_1_pin5[0]), .pin13(n74670_1_pin5[1]));  // open: pin1, pin2, pin3, pin6, pin7, pin15, pin12, pin11, pin10, pin9
  _74670 u_74670_2 (
    .pin4(n74670_1_pin5[1]), .pin5(n74670_1_pin5[0]), .pin14(n74670_1_pin5[0]), .pin13(n74670_1_pin5[1]));  // open: pin1, pin2, pin3, pin6, pin7, pin15, pin12, pin11, pin10, pin9
  _74670 u_74670_3 (
    .pin4(n74670_1_pin5[1]), .pin5(n74670_1_pin5[0]), .pin14(n74670_1_pin5[0]), .pin13(n74670_1_pin5[1]));  // open: pin1, pin2, pin3, pin6, pin7, pin15, pin12, pin11, pin10, pin9
  _74670 u_74670_4 (
    .pin4(n74670_1_pin5[1]), .pin5(n74670_1_pin5[0]), .pin14(n74670_1_pin5[0]), .pin13(n74670_1_pin5[1]));  // open: pin1, pin2, pin3, pin6, pin7, pin15, pin12, pin11, pin10, pin9
endmodule

module registers (
  input  nWE,
  input  nOE,
  input  [2:0] SEL,
  input  [15:0] DIN,
  input  in_5,
  input  GPU_READY,
  input  ZF,
  input  CF,
  input  SF,
  input  CLK,
  output [15:0] DOUT
);

  wire and_1_out, nand_1_out, not_1_out, or_1_out, or_2_out;
  wire [15:4] undriven;

  and and_1 (and_1_out, SEL[0], SEL[1]);
  not not_1 (not_1_out, SEL[2]);
  or or_1 (or_1_out, and_1_out, not_1_out);
  nand nand_1 (nand_1_out, and_1_out, SEL[2]);
  or or_2 (or_2_out, nOE, nand_1_out);
  reg4x16 reg4x16_1 (.nOE(nOE), .nWE(nWE), .nSEL(SEL[2]), .CLK(CLK), .ADDR(SEL[1:0]), .DIN(DIN), .DOUT(DOUT));
  reg4x16 reg4x16_2 (.nOE(nOE), .nWE(nWE), .nSEL(or_1_out), .CLK(CLK), .ADDR(SEL[1:0]), .DIN(DIN), .DOUT(DOUT));
  Logi74173 logi74173_1 (.DIN({undriven, SF, CF, ZF, GPU_READY}), .nWE(1'b0), .CLK(CLK), .nOE(or_2_out), .DOUT(DOUT));
endmodule

module Logi74670 (
  input  nWE,
  input  CLK,
  input  [1:0] ADDR,
  input  [3:0] DIN,
  input  nOE,
  output [3:0] DOUT
);

  wire and_1_out, demultiplexer_1_out0, demultiplexer_1_out1, demultiplexer_1_out2, demultiplexer_1_out3,
       demultiplexer_2_out0, demultiplexer_2_out1, demultiplexer_2_out2, demultiplexer_2_out3, not_1_out,
       not_2_out;
  wire [3:0] register_1_q, register_2_q, register_3_q, register_4_q;

  and and_1 (and_1_out, CLK, not_1_out);
  not not_1 (not_1_out, nWE);
  Demultiplexer #(.select(2)) demultiplexer_1 (
    .out0(demultiplexer_1_out0), .out1(demultiplexer_1_out1), .out2(demultiplexer_1_out2),
    .out3(demultiplexer_1_out3), .in(and_1_out), .sel(ADDR));
  Register #(.trigger("high"), .width(4)) register_1 (
    .D(DIN), .en(demultiplexer_1_out3), .clk(1'b1), .Q(register_1_q));  // open: clr
  Register #(.trigger("high"), .width(4)) register_2 (
    .D(DIN), .en(demultiplexer_1_out2), .clk(1'b1), .Q(register_2_q));  // open: clr
  Register #(.trigger("high"), .width(4)) register_3 (
    .D(DIN), .en(demultiplexer_1_out1), .clk(1'b1), .Q(register_3_q));  // open: clr
  Register #(.trigger("high"), .width(4)) register_4 (
    .D(DIN), .en(demultiplexer_1_out0), .clk(1'b1), .Q(register_4_q));  // open: clr
  assign DOUT = demultiplexer_2_out1 ? register_3_q : 4'bz;  // Controlled_Buffer controlled_buffer_1
  assign DOUT = demultiplexer_2_out0 ? register_4_q : 4'bz;  // Controlled_Buffer controlled_buffer_2
  Demultiplexer #(.select(2)) demultiplexer_2 (
    .out0(demultiplexer_2_out0), .out1(demultiplexer_2_out1), .out2(demultiplexer_2_out2),
    .out3(demultiplexer_2_out3), .in(not_2_out), .sel(ADDR));
  not not_2 (not_2_out, nOE);
  assign DOUT = demultiplexer_2_out3 ? register_1_q : 4'bz;  // Controlled_Buffer controlled_buffer_3
  assign DOUT = demultiplexer_2_out2 ? register_2_q : 4'bz;  // Controlled_Buffer controlled_buffer_4

  // Other names for the same wires on the sheet: ADR[1:0] = ADDR
endmodule

module Logi74173 (
  input  [15:0] DIN,
  input  nWE,
  input  CLK,
  input  nOE,
  output [15:0] DOUT
);

  wire not_1_out, not_2_out;
  wire [15:0] register_1_q;

  not not_1 (not_1_out, nWE);
  Register #(.width(16)) register_1 (.D(DIN), .en(not_1_out), .clk(CLK), .Q(register_1_q));  // open: clr
  assign DOUT = not_2_out ? register_1_q : 16'bz;  // Controlled_Buffer controlled_buffer_1
  not not_2 (not_2_out, nOE);
endmodule
