// Logisim project schematic.circ as structural Verilog
module main (
);

  wire AIA, AIB, ALO, CLK, ctrl_1_iric, MAI, MR, MSL, MW, PCE, PCL, PCO, RGI, RGO, SWP, SWP_STATE;
  wire [2:0] priority_encoder_1_out, RSEL;
  wire [3:0] ALF;
  wire [15:0] alu16_1_o, prgm_counter_1_dout;

  Priority_Encoder priority_encoder_1 (.out(priority_encoder_1_out));  // open: in0, in1, in2, in3, in4, in5, in6, in7, en_in, gs, en_out
  Clock clock_1 (.out(CLK));
  prgm_counter prgm_counter_1 (.PCL(PCL), .PCE(PCE), .CLK(CLK), .DIN(alu16_1_o), .DOUT(prgm_counter_1_dout));
  alu16 alu16_1 (
    .INB(AIB), .B(alu16_1_o), .CLK(CLK), .INA(AIA), .A(alu16_1_o), .FUNC(ALF), .ALUOUT(ALO), .O(alu16_1_o));  // open: Cout
  registers registers_1 (
    .CLK(CLK), .RGO(RGO), .RSEL(RSEL), .RGI(RGI), .DIN(alu16_1_o), .SWP(SWP_STATE), .DOUT(alu16_1_o));  // open: SF, ZF, CF
  J_K_Flip_Flop j_k_ff_1 (.J(SWP), .K(SWP), .Q(SWP_STATE));  // open: clk, Qn, preset, reset
  buffer16 buffer16_1 (.A(prgm_counter_1_dout), .OE(PCO), .B(alu16_1_o));
  // Probe on alu16_1_o
  mem mem_1 (
    .MAL(MAI), .CPU_ADDR(alu16_1_o), .CLK(CLK), .CR(MR), .CW(MW), .RSE(MSL), .SEL(SWP_STATE),
    .CDATAOUT(alu16_1_o));  // open: GADDR, GR, CDATAIN, GDATAOUT0
  ctrl ctrl_1 (
    .IRI(ctrl_1_iric), .CLK(CLK), .IRDI(alu16_1_o), .MW(MW), .MR(MR), .MSL(MSL), .MAI(MAI),
    .IRIC(ctrl_1_iric), .RSEL(RSEL), .RGI(RGI), .RGO(RGO), .INA(AIA), .INB(AIB), .ALF(ALF), .ALO(ALO),
    .PCE(PCE), .PCL(PCL), .PCO(PCO), .SWP(SWP));  // open: HLT, MCR
endmodule

module alu4 (
  input  [3:0] INA,
  input  [3:0] INB,
  input  Cin,
  input  M,
  input  [3:0] S,
  output y,
  output Co,
  output x,
  output eq,
  output [3:0] F
);

  // _74181 74181_1: pin names not known; wires that end beside it: INB[0], INA[0], S[3], S[2], S[1], S[0], Cin, M, F[0], F[1], F[2], INA[1], INB[1], INA[2], INB[2], INA[3], INB[3], y, Co, x, eq, F[3]

  // Other names for the same wires on the sheet: A0 = INA[0]; A1 = INA[1]; A2 = INA[2]; A3 = INA[3]; B0 = INB[0];
  //   B1 = INB[1]; B2 = INB[2]; B3 = INB[3]
endmodule

module alu16 (
  input  INB,
  input  [15:0] B,
  input  CLK,
  input  INA,
  input  [15:0] A,
  input  [3:0] FUNC,
  input  ALUOUT,
  output Cout,
  output [15:0] O
);

  wire alu4_4_co, Cn, Cnx, Cny, Cnz, M, X0, X1, X2, X3, Y0, Y1, Y2, Y3;
  wire [3:0] alu4_1_f, alu4_2_f, alu4_3_f, alu4_4_f, S;
  wire [7:6] rom_1_data;
  wire [15:0] reg16_1_dout, reg16_2_dout;

  ROM #(.addrWidth(4)) rom_1 (.addr(FUNC), .data({rom_1_data, Cn, M, S}));
  reg16 reg16_1 (.DIN(B), .CLK(CLK), .WE(INB), .OE(1'b0), .DOUT(reg16_1_dout));
  reg16 reg16_2 (.DIN(A), .CLK(CLK), .WE(INA), .OE(1'b0), .DOUT(reg16_2_dout));
  alu4 alu4_1 (
    .INA(reg16_2_dout[3:0]), .INB(reg16_1_dout[3:0]), .Cin(Cn), .M(M), .S(S), .y(Y0), .x(X0), .F(alu4_1_f));  // open: Co, eq
  alu4 alu4_2 (
    .INA(reg16_2_dout[7:4]), .INB(reg16_1_dout[7:4]), .Cin(Cnx), .M(M), .S(S), .y(Y1), .x(X1), .F(alu4_2_f));  // open: Co, eq
  alu4 alu4_3 (
    .INA(reg16_2_dout[11:8]), .INB(reg16_1_dout[11:8]), .Cin(Cny), .M(M), .S(S), .y(Y2), .x(X2), .F(alu4_3_f));  // open: Co, eq
  alu4 alu4_4 (
    .INA(reg16_2_dout[15:12]), .INB(reg16_1_dout[15:12]), .Cin(Cnz), .M(M), .S(S), .y(Y3), .Co(alu4_4_co),
    .x(X3), .F(alu4_4_f));  // open: eq
  not not_1 (Cout, alu4_4_co);
  buffer16 buffer16_1 (.A({alu4_4_f, alu4_3_f, alu4_2_f, alu4_1_f}), .OE(ALUOUT), .B(O));
  _74182 u_74182_1 (
    .pin1(Y1), .pin2(X1), .pin3(Y0), .pin4(X0), .pin5(Y3), .pin6(X3), .pin15(X2), .pin14(Y2), .pin13(Cn),
    .pin12(Cnx), .pin11(Cny), .pin9(Cnz));  // open: pin7, pin10

  // Notes on the sheet:
  //   contents of rom_1 (hex, n*v repeats v):
  //   6
endmodule

module mem (
  input  MAL,
  input  CLK,
  input  [15:0] CPU_ADDR,
  input  GR,
  input  [15:0] GADDR,
  input  [15:0] CDATAIN,
  input  SEL,
  input  CR,
  input  CW,
  input  RSE,
  output [15:0] GDATAOUT0,
  output [15:0] CDATAOUT
);

  wire not_1_out, not_2_out, or_1_out, or_2_out, or_3_out, or_4_out, or_5_out;
  wire [15:0] reg16_1_dout, rom_1_data;

  reg16 reg16_1 (.DIN(CPU_ADDR), .CLK(CLK), .WE(MAL), .OE(1'b0), .DOUT(reg16_1_dout));
  or or_1 (or_1_out, CR, not_1_out);
  not not_1 (not_1_out, RSE);
  or or_2 (or_2_out, not_2_out, RSE, CR);
  or or_3 (or_3_out, not_2_out, RSE, CW);
  not not_2 (not_2_out, reg16_1_dout[15]);
  or or_4 (or_4_out, reg16_1_dout[15], RSE, CW);
  or or_5 (or_5_out, reg16_1_dout[15], RSE, CR);
  ROM #(.addrWidth(16), .dataWidth(16)) rom_1 (.addr(reg16_1_dout), .data(rom_1_data));
  IS61 is61_1 (.ADDR(reg16_1_dout[14:0]), .WE(or_4_out), .OE(or_5_out), .DIN(CDATAIN), .DOUT(CDATAOUT));
  double_buffer double_buffer_1 (
    .ADDR0(reg16_1_dout), .ADDR1(GADDR), .R1(GR), .R0(or_2_out), .W1(1'b0), .W0(or_3_out), .SEL(SEL),
    .DATAIN0(CDATAIN), .DATAOUT0(CDATAOUT), .DATAOUT1(GDATAOUT0));  // open: DATAIN1
  buffer16 buffer16_1 (.A(rom_1_data), .OE(or_1_out), .B(CDATAOUT));

  // Notes on the sheet:
  //   contents of rom_1 (hex, n*v repeats v):
  //   c20 1111
endmodule

module IS61 (
  input  [15:0] DIN,
  input  [14:0] ADDR,
  input  WE,
  input  OE,
  output [15:0] DOUT
);

  wire and_1_out, not_1_out, not_2_out;
  wire [15:0] controlled_buffer_1_out;

  not not_1 (not_1_out, OE);
  RAM #(.addrWidth(15), .dataWidth(16), .databus("bidir"), .trigger("high")) ram_1 (
    .addr(ADDR), .we(not_2_out), .oe(and_1_out));  // open: clk, data
  not not_2 (not_2_out, WE);
  and and_1 (and_1_out, WE, not_1_out);
  assign controlled_buffer_1_out = not_2_out ? DIN : 16'bz;  // Controlled_Buffer controlled_buffer_1
  assign DOUT = and_1_out ? controlled_buffer_1_out : 16'bz;  // Controlled_Buffer controlled_buffer_2
endmodule

module dbel (
  input  SEL,
  input  [15:0] ADDR0,
  input  [15:0] ADDR1,
  input  R1,
  input  R0,
  input  W1,
  input  W0,
  input  [15:0] DATAIN0,
  input  [15:0] DATAIN1,
  output [15:0] DATAOUT0,
  output [15:0] DATAOUT1
);

  wire and_1_out, and_2_out, E0, E1, not_1_out, not_2_out, not_3_out, not_4_out, R, W;
  wire [15:0] ADDR, bidirectional_buffer16_2_b_out, controlled_buffer_1_out, is61_1_dout;

  not not_1 (not_1_out, SEL);
  buffer16 buffer16_1 (.A(ADDR0), .OE(SEL), .B(ADDR));
  buffer16 buffer16_2 (.A(ADDR1), .OE(not_1_out), .B(ADDR));
  IS61 is61_1 (.ADDR(ADDR[14:0]), .WE(W), .OE(R), .DIN(is61_1_dout), .DOUT(is61_1_dout));
  Multiplexer multiplexer_1 (.in0(W0), .in1(W1), .out(W), .sel(SEL));
  Multiplexer multiplexer_2 (.in0(R0), .in1(R1), .out(R), .sel(SEL));
  assign controlled_buffer_1_out = not_2_out ? DATAIN0 : 16'bz;  // Controlled_Buffer controlled_buffer_1
  bidirectional_buffer16 bidirectional_buffer16_1 (
    .OE(E0), .DIR(W0), .A_IN(is61_1_dout), .B_IN(controlled_buffer_1_out), .B_OUT(controlled_buffer_1_out),
    .A_OUT(is61_1_dout));
  not not_2 (not_2_out, W0);
  bidirectional_buffer16 bidirectional_buffer16_2 (
    .OE(E1), .DIR(W1), .A_IN(is61_1_dout), .B_IN(bidirectional_buffer16_2_b_out),
    .B_OUT(bidirectional_buffer16_2_b_out), .A_OUT(is61_1_dout));
  and and_1 (and_1_out, R1, W1);
  and and_2 (and_2_out, R0, W0);
  assign DATAOUT0 = W0 ? controlled_buffer_1_out : 16'bz;  // Controlled_Buffer controlled_buffer_2
  assign bidirectional_buffer16_2_b_out = not_3_out ? DATAIN1 : 16'bz;  // Controlled_Buffer controlled_buffer_3
  assign DATAOUT1 = W1 ? bidirectional_buffer16_2_b_out : 16'bz;  // Controlled_Buffer controlled_buffer_4
  not not_3 (not_3_out, W1);
  not not_4 (not_4_out, SEL);
  or or_1 (E0, SEL, and_2_out);
  or or_2 (E1, and_1_out, not_4_out);
endmodule

module buffer16 (
  input  [15:0] A,
  input  OE,
  output [15:0] B
);

  wire not_1_out;

  not not_1 (not_1_out, OE);
  assign B = not_1_out ? A : 16'bz;  // Controlled_Buffer controlled_buffer_1

  // Notes on the sheet:
  //   OE: pull=up
endmodule

module buffer15 (
  input  [14:0] A,
  input  OE,
  output [14:0] B
);

  wire not_1_out;

  assign B = not_1_out ? A : 15'bz;  // Controlled_Buffer controlled_buffer_1
  not not_1 (not_1_out, OE);
endmodule

module double_buffer (
  input  [15:0] DATAIN1,
  input  [15:0] DATAIN0,
  input  SEL,
  input  [15:0] ADDR0,
  input  [15:0] ADDR1,
  input  R1,
  input  R0,
  input  W1,
  input  W0,
  output [15:0] DATAOUT0,
  output [15:0] DATAOUT1
);

  wire not_1_out;

  not not_1 (not_1_out, SEL);
  dbel dbel_1 (
    .SEL(SEL), .ADDR0(ADDR0), .ADDR1(ADDR1), .R1(R1), .R0(R0), .W1(W1), .W0(W0), .DATAIN0(DATAIN0),
    .DATAIN1(DATAIN1), .DATAOUT0(DATAOUT0), .DATAOUT1(DATAOUT1));
  dbel dbel_2 (
    .SEL(not_1_out), .ADDR0(ADDR0), .ADDR1(ADDR1), .R1(R1), .R0(R0), .W1(W1), .W0(W0), .DATAIN0(DATAIN0),
    .DATAIN1(DATAIN1), .DATAOUT0(DATAOUT0), .DATAOUT1(DATAOUT1));
endmodule

module bidirectional_buffer16 (
  input  DIR,
  input  OE,
  input  [15:0] A_IN,
  input  [15:0] B_IN,
  output [15:0] B_OUT,
  output [15:0] A_OUT
);

  wire and_1_out, and_2_out, not_1_out, not_2_out;

  not not_1 (not_1_out, OE);
  not not_2 (not_2_out, DIR);
  and and_1 (and_1_out, not_2_out, not_1_out);
  assign A_OUT = and_1_out ? B_IN : 16'bz;  // Controlled_Buffer controlled_buffer_1
  and and_2 (and_2_out, DIR, not_1_out);
  assign B_OUT = and_2_out ? A_IN : 16'bz;  // Controlled_Buffer controlled_buffer_2
endmodule

module SST39SF010A (
  input  [16:0] ADDR,
  input  OE,
  output [7:0] DOUT
);

  wire not_1_out;
  wire [7:0] rom_1_data;

  ROM #(.addrWidth(17)) rom_1 (.addr(ADDR), .data(rom_1_data));
  assign DOUT = not_1_out ? rom_1_data : 8'bz;  // Controlled_Buffer controlled_buffer_1
  not not_1 (not_1_out, OE);

  // Notes on the sheet:
  //   contents of rom_1 (hex, n*v repeats v):
  //   4
endmodule

module reg16 (
  input  WE,
  input  [15:0] DIN,
  input  CLK,
  input  OE,
  output [15:0] DOUT
);

  wire not_1_out, not_2_out;
  wire [15:0] register_1_q;

  Register #(.width(16)) register_1 (.D(DIN), .en(not_1_out), .clk(CLK), .Q(register_1_q));  // open: clr
  not not_1 (not_1_out, WE);
  assign DOUT = not_2_out ? register_1_q : 16'bz;  // Controlled_Buffer controlled_buffer_1
  not not_2 (not_2_out, OE);
endmodule

module prgm_counter (
  input  PCL,
  input  PCE,
  input  CLK,
  input  [15:0] DIN,
  output [15:0] DOUT
);

  wire not_1_out;

  not not_1 (not_1_out, PCL);
  Counter #(.max('hffff), .width(16)) counter_1 (
    .load(not_1_out), .up(1'b1), .count(PCE), .clk(CLK), .D(DIN), .Q(DOUT));  // open: clr, carry
endmodule

module ctrl (
  input  IRI,
  input  [15:0] IRDI,
  input  CLK,
  output MW,
  output MR,
  output MSL,
  output MAI,
  output IRIC,
  output [2:0] RSEL,
  output RGI,
  output RGO,
  output INA,
  output INB,
  output [3:0] ALF,
  output ALO,
  output PCE,
  output PCL,
  output PCO,
  output HLT,
  output MCR,
  output SWP
);

  wire n74161_1_pin2, n74161_1_pin7, n74161_1_pin10;
  wire [3:0] n74161_1_pin14;
  wire [15:0] reg16_1_dout;
  wire [23:23] rom_1_data;

  _74161 u_74161_1 (
    .pin1(MCR), .pin2(n74161_1_pin2), .pin7(n74161_1_pin7), .pin14(n74161_1_pin14[0]),
    .pin13(n74161_1_pin14[1]), .pin12(n74161_1_pin14[2]), .pin11(n74161_1_pin14[3]), .pin10(n74161_1_pin10),
    .pin9(n74161_1_pin10));  // open: pin3, pin4, pin5, pin6, pin15
  not not_1 (n74161_1_pin2, CLK);
  reg16 reg16_1 (.DIN(IRDI), .CLK(CLK), .WE(IRI), .OE(1'b0), .DOUT(reg16_1_dout));
  // Probe on reg16_1_dout[13:0]
  // Probe on {reg16_1_dout[13:0], n74161_1_pin14}
  ROM #(.addrWidth(18), .dataWidth(24)) rom_1 (
    .addr({reg16_1_dout[13:0], n74161_1_pin14}),
    .data({rom_1_data[23], SWP, MCR, HLT, PCO, PCL, PCE, ALO, ALF, INB, INA, RGO, RGI, RSEL, IRIC, MAI, MSL, MR, MW}));
  // also tied to VCC on the sheet: {n74161_1_pin10, n74161_1_pin7}

  // Notes on the sheet:
  //   contents of rom_1 (hex, n*v repeats v):
  //   250c13 2f0c0d 49278*2d0c1b 250c13 2f0c0d 250c13 2f0c15 2d0e1a d0c1b d0c1b d0c1b 120*2d0c1b 250c13
  //   2f0c0d 2d0e13 2d0e1a d0c1b d0c1b d0c1b 9*2d0c1b 250c13 2f0c0d 2d0e33 2d0e1a d0c1b d0c1b d0c1b
  //   9*2d0c1b 250c13 2f0c0d 2d0e53 2d0e1a d0c1b d0c1b d0c1b 9*2d0c1b 250c13 2f0c0d 2d0e73 2d0e1a d0c1b
  //   d0c1b d0c1b 9*2d0c1b 250c13 2f0c0d 2d0e93 2d0e1a d0c1b d0c1b d0c1b 9*2d0c1b 250c13 2f0c0d 2d0eb3
  //   2d0e1a d0c1b d0c1b d0c1b 9*2d0c1b 250c13 2f0c0d 2d0ed3 2d0e1a d0c1b d0c1b d0c1b 9*2d0c1b 250c13
  //   2f0c0d 2d0ef3 2d0e1a d0c1b d0c1b d0c1b 137*2d0c1b 250c13 2f0c0d 250c13 2f0d1d d0c1b d0c1b d0c1b
  //   121*2d0c1b 250c13 2f0c0d 250c13 2f0c15 2d0d19 d0c1b d0c1b d0c1b 120*2d0c1b 250c13 2f0c0d 2d0e13
  //   2d0d19 d0c1b d0c1b d0c1b 9*2d0c1b 250c13 2f0c0d 2d0e33 2d0d19 d0c1b d0c1b d0c1b 9*2d0c1b 250c13
  //   2f0c0d 2d0e53 2d0d19 d0c1b d0c1b d0c1b 9*2d0c1b 250c13 2f0c0d 2d0e73 2d0d19 d0c1b d0c1b d0c1b
  //   9*2d0c1b 250c13 2f0c0d 2d0e93 2d0d19 d0c1b d0c1b d0c1b 9*2d0c1b 250c13 2f0c0d 2d0eb3 2d0d19 d0c1b
  //   d0c1b d0c1b 9*2d0c1b 250c13 2f0c0d 2d0ed3 2d0d19 d0c1b d0c1b d0c1b 9*2d0c1b 250c13 2f0c0d 2d0ef3
  //   2d0d19 d0c1b d0c1b d0c1b 265*2d0c1b 250c13 2f0c0d 250c13 2f0c15 2d0e3a d0c1b d0c1b d0c1b 120*2d0c1b
  //   250c13 2f0c0d 2d0e13 2d0e3a d0c1b d0c1b d0c1b 9*2d0c1b 250c13 2f0c0d 2d0e33 2d0e3a d0c1b d0c1b d0c1b
  //   9*2d0c1b 250c13 2f0c0d 2d0e53 2d0e3a d0c1b d0c1b d0c1b 9*2d0c1b 250c13 2f0c0d 2d0e73 2d0e3a d0c1b
  //   d0c1b d0c1b 9*2d0c1b 250c13 2f0c0d 2d0e93 2d0e3a d0c1b d0c1b d0c1b 9*2d0c1b 250c13 2f0c0d 2d0eb3
  //   2d0e3a d0c1b d0c1b d0c1b 9*2d0c1b 250c13 2f0c0d 2d0ed3 2d0e3a d0c1b d0c1b d0c1b 9*2d0c1b 250c13
  //   2f0c0d 2d0ef3 2d0e3a d0c1b d0c1b d0c1b 137*2d0c1b 250c13 2f0c0d 250c13 2f0d3d d0c1b d0c1b d0c1b
  //   121*2d0c1b 250c13 2f0c0d 250c13 2f0c15 2d0d39 d0c1b d0c1b d0c1b 120*2d0c1b 250c13 2f0c0d 2d0e13
  //   2d0d39 d0c1b d0c1b d0c1b 9*2d0c1b 250c13 2f0c0d 2d0e33 2d0d39 d0c1b d0c1b d0c1b 9*2d0c1b 250c13
  //   2f0c0d 2d0e53 2d0d39 d0c1b d0c1b d0c1b 9*2d0c1b 250c13 2f0c0d 2d0e73 2d0d39 d0c1b d0c1b d0c1b
  //   9*2d0c1b 250c13 2f0c0d 2d0e93 2d0d39 d0c1b d0c1b d0c1b 9*2d0c1b 250c13 2f0c0d 2d0eb3 2d0d39 d0c1b
  //   d0c1b d0c1b 9*2d0c1b 250c13 2f0c0d 2d0ed3 2d0d39 d0c1b d0c1b d0c1b 9*2d0c1b 250c13 2f0c0d 2d0ef3
  //   2d0d39 d0c1b d0c1b d0c1b 265*2d0c1b 250c13 2f0c0d 250c13 2f0c15 2d0e5a d0c1b d0c1b d0c1b 120*2d0c1b
  //   250c13 2f0c0d 2d0e13 2d0e5a d0c1b d0c1b d0c1b 9*2d0c1b 250c13 2f0c0d 2d0e33 2d0e5a d0c1b d0c1b d0c1b
  //   9*2d0c1b 250c13 2f0c0d 2d0e53 2d0e5a d0c1b d0c1b d0c1b 9*2d0c1b 250c13 2f0c0d 2d0e73 2d0e5a d0c1b
  //   d0c1b d0c1b 9*2d0c1b 250c13 2f0c0d 2d0e93 2d0e5a d0c1b d0c1b d0c1b 9*2d0c1b 250c13 2f0c0d 2d0eb3
  //   2d0e5a d0c1b d0c1b d0c1b 9*2d0c1b 250c13 2f0c0d 2d0ed3 2d0e5a d0c1b d0c1b d0c1b 9*2d0c1b 250c13
  //   2f0c0d 2d0ef3 2d0e5a d0c1b d0c1b d0c1b 137*2d0c1b 250c13 2f0c0d 250c13 2f0d5d d0c1b d0c1b d0c1b
  //   121*2d0c1b 250c13 2f0c0d 250c13 2f0c15 2d0d59 d0c1b d0c1b d0c1b 120*2d0c1b 250c13 2f0c0d 2d0e13
  //   2d0d59 d0c1b d0c1b d0c1b 9*2d0c1b 250c13 2f0c0d 2d0e33 2d0d59 d0c1b d0c1b d0c1b 9*2d0c1b 250c13
  //   2f0c0d 2d0e53 2d0d59 d0c1b d0c1b d0c1b 9*2d0c1b 250c13 2f0c0d 2d0e73 2d0d59 d0c1b d0c1b d0c1b
  //   9*2d0c1b 250c13 2f0c0d 2d0e93 2d0d59 d0c1b d0c1b d0c1b 9*2d0c1b 250c13 2f0c0d 2d0eb3 2d0d59 d0c1b
  //   d0c1b d0c1b 9*2d0c1b 250c13 2f0c0d 2d0ed3 2d0d59 d0c1b d0c1b d0c1b 9*2d0c1b 250c13 2f0c0d 2d0ef3
  //   2d0d59 d0c1b d0c1b d0c1b 265*2d0c1b 250c13 2f0c0d 250c13 2f0c15 2d0e7a d0c1b d0c1b d0c1b 120*2d0c1b
  //   250c13 2f0c0d 2d0e13 2d0e7a d0c1b d0c1b d0c1b 9*2d0c1b 250c13 2f0c0d 2d0e33 2d0e7a d0c1b d0c1b d0c1b
  //   9*2d0c1b 250c13 2f0c0d 2d0e53 2d0e7a d0c1b d0c1b d0c1b 9*2d0c1b 250c13 2f0c0d 2d0e73 2d0e7a d0c1b
  //   d0c1b d0c1b 9*2d0c1b 250c13 2f0c0d 2d0e93 2d0e7a d0c1b d0c1b d0c1b 9*2d0c1b 250c13 2f0c0d 2d0eb3
  //   2d0e7a d0c1b d0c1b d0c1b 9*2d0c1b 250c13 2f0c0d 2d0ed3 2d0e7a d0c1b d0c1b d0c1b 9*2d0c1b 250c13
  //   2f0c0d 2d0ef3 2d0e7a d0c1b d0c1b d0c1b 137*2d0c1b 250c13 2f0c0d 250c13 2f0d7d d0c1b d0c1b d0c1b
  //   121*2d0c1b 250c13 2f0c0d 250c13 2f0c15 2d0d79 d0c1b d0c1b d0c1b 120*2d0c1b 250c13 2f0c0d 2d0e13
  //   2d0d79 d0c1b d0c1b d0c1b 9*2d0c1b 250c13 2f0c0d 2d0e33 2d0d79 d0c1b d0c1b d0c1b 9*2d0c1b 250c13
  //   2f0c0d 2d0e53 2d0d79 d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
endmodule

module registers (
  input  CLK,
  input  RGO,
  input  [2:0] RSEL,
  input  [15:0] DIN,
  input  SF,
  input  ZF,
  input  CF,
  input  SWP,
  input  RGI,
  output [15:0] DOUT
);

  wire decoder_1_out0, decoder_1_out1, decoder_1_out2, decoder_1_out3, decoder_1_out4, decoder_1_out5,
       decoder_1_out6, decoder_1_out7, decoder_2_out0, decoder_2_out1, decoder_2_out2, decoder_2_out3,
       decoder_2_out4, decoder_2_out5, decoder_2_out6, not_1_out, not_2_out, not_3_out, not_4_out, not_5_out,
       not_6_out, not_7_out, not_8_out, not_9_out, not_10_out, not_11_out, not_12_out, not_13_out,
       not_14_out, not_15_out;
  wire [15:4] undriven;

  Decoder #(.select(3)) decoder_1 (
    .out0(decoder_1_out0), .out1(decoder_1_out1), .out2(decoder_1_out2), .out3(decoder_1_out3),
    .out4(decoder_1_out4), .out5(decoder_1_out5), .out6(decoder_1_out6), .out7(decoder_1_out7), .sel(RSEL),
    .en(RGO));
  not not_1 (not_1_out, decoder_1_out1);
  not not_2 (not_2_out, decoder_1_out0);
  not not_3 (not_3_out, decoder_1_out3);
  not not_4 (not_4_out, decoder_1_out5);
  not not_5 (not_5_out, decoder_1_out7);
  not not_6 (not_6_out, decoder_1_out2);
  not not_7 (not_7_out, decoder_1_out4);
  not not_8 (not_8_out, decoder_1_out6);
  not not_9 (not_9_out, decoder_2_out0);
  Decoder #(.select(3)) decoder_2 (
    .out0(decoder_2_out0), .out1(decoder_2_out1), .out2(decoder_2_out2), .out3(decoder_2_out3),
    .out4(decoder_2_out4), .out5(decoder_2_out5), .out6(decoder_2_out6), .sel(RSEL), .en(RGI));  // open: out7
  not not_10 (not_10_out, decoder_2_out1);
  not not_11 (not_11_out, decoder_2_out3);
  not not_12 (not_12_out, decoder_2_out5);
  not not_13 (not_13_out, decoder_2_out2);
  not not_14 (not_14_out, decoder_2_out4);
  not not_15 (not_15_out, decoder_2_out6);
  reg16 reg16_1 (.DIN(DIN), .CLK(CLK), .WE(not_9_out), .OE(not_2_out), .DOUT(DOUT));
  reg16 reg16_2 (.DIN(DIN), .CLK(CLK), .WE(not_10_out), .OE(not_1_out), .DOUT(DOUT));
  reg16 reg16_3 (.DIN(DIN), .CLK(CLK), .WE(not_13_out), .OE(not_6_out), .DOUT(DOUT));
  reg16 reg16_4 (.DIN(DIN), .CLK(CLK), .WE(not_11_out), .OE(not_3_out), .DOUT(DOUT));
  reg16 reg16_5 (.DIN(DIN), .CLK(CLK), .WE(not_14_out), .OE(not_7_out), .DOUT(DOUT));
  reg16 reg16_6 (.DIN(DIN), .CLK(CLK), .WE(not_12_out), .OE(not_4_out), .DOUT(DOUT));
  reg16 reg16_7 (.DIN(DIN), .CLK(CLK), .WE(not_15_out), .OE(not_8_out), .DOUT(DOUT));
  reg16 reg16_8 (.DIN({undriven, SWP, CF, ZF, SF}), .CLK(CLK), .WE(1'b0), .OE(not_5_out), .DOUT(DOUT));
endmodule
