// Digital circuit 74ls670.dig as structural Verilog
module _74ls670 (
  input  [3:0] DIN,
  input  [1:0] ADDR,
  input  nWE,
  input  nOE,
  output [3:0] DOUT
);

  _74670 _74670_1 (
    .pin1(DIN[1]), .pin2(DIN[2]), .pin3(DIN[3]), .pin4(ADDR[1]), .pin5(ADDR[0]), .pin6(DOUT[3]),
    .pin7(DOUT[2]), .pin8(1'b0), .pin9(DOUT[1]), .pin10(DOUT[0]), .pin11(nOE), .pin12(nWE), .pin13(ADDR[1]),
    .pin14(ADDR[0]), .pin15(DIN[0]), .pin16(1'b1));
endmodule
