// Digital circuit alu16.dig as structural Verilog
module alu16 (
  input  [15:0] A,
  input  nINA,
  input  [15:0] B,
  input  nINB,
  input  [3:0] S,
  input  M,
  input  nCn,
  input  CLK,
  input  nALUOUT,
  output [15:0] O,
  output Cout
);

  wire alu4_4_co, Cnx, Cny, Cnz, x0, x1, x2, x3, y0, y1, y2, y3;
  wire [3:0] alu4_1_f, alu4_2_f, alu4_3_f, alu4_4_f;
  wire [15:0] reg16_1_dout, reg16_2_dout;

  reg16 reg16_1 (.nWE(nINB), .CLK(CLK), .DIN(B), .nOE(1'b0), .DOUT(reg16_1_dout));
  reg16 reg16_2 (.nWE(nINA), .CLK(CLK), .DIN(A), .nOE(1'b0), .DOUT(reg16_2_dout));
  // Probe on reg16_1_dout
  // Probe on reg16_2_dout
  alu4 alu4_1 (
    .INA(reg16_2_dout[3:0]), .INB(reg16_1_dout[3:0]), .Cin(nCn), .M(M), .S(S), .x(x0), .y(y0), .F(alu4_1_f));  // open: Co, eq
  alu4 alu4_2 (
    .INA(reg16_2_dout[7:4]), .INB(reg16_1_dout[7:4]), .Cin(Cnx), .M(M), .S(S), .x(x1), .y(y1), .F(alu4_2_f));  // open: Co, eq
  alu4 alu4_3 (
    .INA(reg16_2_dout[11:8]), .INB(reg16_1_dout[11:8]), .Cin(Cny), .M(M), .S(S), .x(x2), .y(y2), .F(alu4_3_f));  // open: Co, eq
  alu4 alu4_4 (
    .INA(reg16_2_dout[15:12]), .INB(reg16_1_dout[15:12]), .Cin(Cnz), .M(M), .S(S), .x(x3), .Co(alu4_4_co),
    .y(y3), .F(alu4_4_f));  // open: eq
  not not_1 (Cout, alu4_4_co);
  _74182 _74182_1 (
    .pin1(y1), .pin2(x1), .pin3(y0), .pin4(x0), .pin5(y3), .pin6(x3), .pin8(1'b0), .pin9(Cnz), .pin11(Cny),
    .pin12(Cnx), .pin13(nCn), .pin14(y2), .pin15(x2), .pin16(1'b1));  // open: pin7, pin10
  assign O = ~nALUOUT ? {alu4_4_f, alu4_3_f, alu4_2_f, alu4_1_f} : 16'bz;  // DriverInvSel driverinvsel_1

  // Other names for the same wires on the sheet: Cn = nCn
endmodule
