// Digital circuit alu4.dig as structural Verilog
module alu4 (
  input  [3:0] INA,
  input  [3:0] INB,
  input  Cin,
  input  M,
  input  [3:0] S,
  output x,
  output Co,
  output y,
  output eq,
  output [3:0] F
);

  _74181 _74181_1 (
    .pin1(INB[0]), .pin2(INA[0]), .pin3(S[3]), .pin4(S[2]), .pin5(S[1]), .pin6(S[0]), .pin7(Cin), .pin8(M),
    .pin9(F[0]), .pin10(F[1]), .pin11(F[2]), .pin12(1'b0));  // open: pin13, pin14, pin15, pin16, pin17, pin18, pin19, pin20, pin21, pin22, pin23, pin24

  // Other names for the same wires on the sheet: A0 = INA[0]; A1 = INA[1]; A2 = INA[2]; A3 = INA[3]; B0 = INB[0];
  //   B1 = INB[1]; B2 = INB[2]; B3 = INB[3]
endmodule
