// Digital circuit bidirectional_buffer_16.dig as structural Verilog
module bidirectional_buffer_16 (
  input  [15:0] A,
  input  nOE,
  input  A2B,
  output [15:0] B
);

  wire _74245_1_pin11, _74245_1_pin12, _74245_1_pin13, _74245_1_pin14, _74245_1_pin15, _74245_1_pin16,
       _74245_1_pin17, _74245_1_pin18, _74245_2_pin11, _74245_2_pin12, _74245_2_pin13, _74245_2_pin14,
       _74245_2_pin15, _74245_2_pin16, _74245_2_pin17, _74245_2_pin18, bussplitter_1_d0, bussplitter_1_d1,
       bussplitter_1_d2, bussplitter_1_d3, bussplitter_1_d4, bussplitter_1_d5, bussplitter_1_d6,
       bussplitter_1_d7, bussplitter_1_d8, bussplitter_1_d9, bussplitter_1_d10, bussplitter_1_d11,
       bussplitter_1_d12, bussplitter_1_d13, bussplitter_1_d14, bussplitter_1_d15, not_1_out;

  BusSplitter #(.Bits(16)) bussplitter_1 (
    .D(A), .OE(A2B), .D0(bussplitter_1_d0), .D1(bussplitter_1_d1), .D2(bussplitter_1_d2),
    .D3(bussplitter_1_d3), .D4(bussplitter_1_d4), .D5(bussplitter_1_d5), .D6(bussplitter_1_d6),
    .D7(bussplitter_1_d7), .D8(bussplitter_1_d8), .D9(bussplitter_1_d9), .D10(bussplitter_1_d10),
    .D11(bussplitter_1_d11), .D12(bussplitter_1_d12), .D13(bussplitter_1_d13), .D14(bussplitter_1_d14),
    .D15(bussplitter_1_d15));
  _74245 _74245_1 (
    .pin1(A2B), .pin2(bussplitter_1_d0), .pin3(bussplitter_1_d1), .pin4(bussplitter_1_d2),
    .pin5(bussplitter_1_d3), .pin6(bussplitter_1_d4), .pin7(bussplitter_1_d5), .pin8(bussplitter_1_d6),
    .pin9(bussplitter_1_d7), .pin10(1'b0), .pin11(_74245_1_pin11), .pin12(_74245_1_pin12),
    .pin13(_74245_1_pin13), .pin14(_74245_1_pin14), .pin15(_74245_1_pin15), .pin16(_74245_1_pin16),
    .pin17(_74245_1_pin17), .pin18(_74245_1_pin18), .pin19(nOE), .pin20(1'b1));
  _74245 _74245_2 (
    .pin1(A2B), .pin2(bussplitter_1_d8), .pin3(bussplitter_1_d9), .pin4(bussplitter_1_d10),
    .pin5(bussplitter_1_d11), .pin6(bussplitter_1_d12), .pin7(bussplitter_1_d13), .pin8(bussplitter_1_d14),
    .pin9(bussplitter_1_d15), .pin10(1'b0), .pin11(_74245_2_pin11), .pin12(_74245_2_pin12),
    .pin13(_74245_2_pin13), .pin14(_74245_2_pin14), .pin15(_74245_2_pin15), .pin16(_74245_2_pin16),
    .pin17(_74245_2_pin17), .pin18(_74245_2_pin18), .pin19(nOE), .pin20(1'b1));
  BusSplitter #(.Bits(16)) bussplitter_2 (
    .D(B), .OE(not_1_out), .D0(_74245_1_pin18), .D1(_74245_1_pin17), .D2(_74245_1_pin16),
    .D3(_74245_1_pin15), .D4(_74245_1_pin14), .D5(_74245_1_pin13), .D6(_74245_1_pin12), .D7(_74245_1_pin11),
    .D8(_74245_2_pin18), .D9(_74245_2_pin17), .D10(_74245_2_pin16), .D11(_74245_2_pin15),
    .D12(_74245_2_pin14), .D13(_74245_2_pin13), .D14(_74245_2_pin12), .D15(_74245_2_pin11));
  not not_1 (not_1_out, A2B);
  // Pins of 1 and 16 bits meet at B
endmodule
