// Digital circuit double_buffer_el.dig as structural Verilog
module double_buffer_el (
  input  SEL,
  input  [14:0] ADDR0,
  input  W0,
  input  R0,
  input  [14:0] ADDR1,
  input  W1,
  input  R1,
  input  [15:0] DATA0,
  input  [15:0] DATA1
);

  wire and_1_out, and_2_out, E0, E1, not_1_out, not_2_out, R, W;
  wire [14:0] ADDR;
  wire [15:0] bidirectional_buffer_16_1_p1;

  assign ADDR = ~not_1_out ? ADDR1 : 15'bz;  // DriverInvSel driverinvsel_1
  not not_1 (not_1_out, SEL);
  assign ADDR = ~SEL ? ADDR0 : 15'bz;  // DriverInvSel driverinvsel_2
  Multiplexer multiplexer_1 (.sel(SEL), .in_0(R0), .in_1(R1), .out(R));
  Multiplexer multiplexer_2 (.sel(SEL), .in_0(W0), .in_1(W1), .out(W));
  ramchip ramchip_1 (.nWE(W), .D(bidirectional_buffer_16_1_p1), .nOE(R), .ADDR(ADDR));
  and and_1 (and_1_out, R0, W0);
  not not_2 (not_2_out, SEL);
  and and_2 (and_2_out, R1, W1);
  // bidirectional_buffer_16 bidirectional_buffer_16_1: pin names not known; wires that end beside it: bidirectional_buffer_16_1_p1, E0, W0, DATA0
  // bidirectional_buffer_16 bidirectional_buffer_16_2: pin names not known; wires that end beside it: bidirectional_buffer_16_1_p1, E1, W1, DATA1
  or or_1 (E0, and_1_out, SEL);
  or or_2 (E1, not_2_out, and_2_out);

  // Notes on the sheet:
  //   W0: default 1
  //   R0: default 1
  //   W1: default 1
  //   R1: default 1
endmodule
