// Digital circuit gpu.dig as structural Verilog
module gpu (
  input  [15:0] VDATA,
  input  PC,
  output [4:0] R,
  output [4:0] G,
  output [4:0] B,
  output HSYNC,
  output nVOE,
  output VSYNC,
  output [14:0] VADDR
);

  wire _74161_1_pin12, _74161_2_pin15, _74161_4_pin15, _74161_5_pin15, A0, A1, and_1_out, LE, nA0, nA1, nA2,
       nA3, nA4, nand_1_out, nand_2_out, nand_4_out, nand_5_out, nand_6_out, nand_8_out, nB0, nB1, nB2, nB3,
       nB4, nB5, nB6, nB7, nOE_H, nOE_V, not_1_out, nVR;

  not not_1 (not_1_out, _74161_1_pin12);
  _74161 _74161_1 (
    .pin1(not_1_out), .pin2(PC), .pin3(1'b0), .pin4(1'b0), .pin5(1'b0), .pin6(1'b0), .pin7(1'b1),
    .pin8(1'b0), .pin9(1'b1), .pin10(1'b1), .pin12(_74161_1_pin12), .pin16(1'b1));  // open: pin11, pin13, pin14, pin15
  _74161 _74161_2 (
    .pin1(LE), .pin2(_74161_1_pin12), .pin3(1'b0), .pin4(1'b0), .pin5(1'b0), .pin6(1'b0), .pin7(1'b1),
    .pin8(1'b0), .pin9(1'b1), .pin10(1'b1), .pin11(VADDR[3]), .pin12(VADDR[2]), .pin13(VADDR[1]),
    .pin14(VADDR[0]), .pin15(_74161_2_pin15), .pin16(1'b1));
  _74161 _74161_3 (
    .pin1(LE), .pin2(_74161_1_pin12), .pin3(1'b0), .pin4(1'b0), .pin5(1'b0), .pin6(1'b0), .pin7(1'b1),
    .pin8(1'b0), .pin9(1'b1), .pin10(_74161_2_pin15), .pin11(VADDR[7]), .pin12(VADDR[6]), .pin13(VADDR[5]),
    .pin14(VADDR[4]), .pin16(1'b1));  // open: pin15
  _74161 _74161_4 (
    .pin1(nVR), .pin2(LE), .pin3(1'b0), .pin4(1'b0), .pin5(1'b0), .pin6(1'b0), .pin7(1'b1), .pin8(1'b0),
    .pin9(1'b1), .pin10(1'b1), .pin11(VADDR[9]), .pin12(VADDR[8]), .pin13(A1), .pin14(A0),
    .pin15(_74161_4_pin15), .pin16(1'b1));
  _74161 _74161_5 (
    .pin1(nVR), .pin2(LE), .pin3(1'b0), .pin4(1'b0), .pin5(1'b0), .pin6(1'b0), .pin7(1'b1), .pin8(1'b0),
    .pin9(1'b1), .pin10(_74161_4_pin15), .pin11(VADDR[13]), .pin12(VADDR[12]), .pin13(VADDR[11]),
    .pin14(VADDR[10]), .pin15(_74161_5_pin15), .pin16(1'b1));
  _74161 _74161_6 (
    .pin1(nVR), .pin2(LE), .pin3(1'b0), .pin4(1'b0), .pin5(1'b0), .pin6(1'b0), .pin7(1'b1), .pin8(1'b0),
    .pin9(1'b1), .pin10(_74161_5_pin15), .pin14(VADDR[14]), .pin16(1'b1));  // open: pin11, pin12, pin13, pin15
  not not_2 (nB0, VADDR[0]);
  not not_3 (nB1, VADDR[1]);
  not not_4 (nB2, VADDR[2]);
  not not_5 (nB3, VADDR[3]);
  not not_6 (nB4, VADDR[4]);
  not not_7 (nB5, VADDR[5]);
  not not_8 (nB6, VADDR[6]);
  not not_9 (nB7, VADDR[7]);
  not not_10 (nA0, A0);
  not not_11 (nA1, A1);
  not not_12 (nA2, VADDR[8]);
  not not_13 (nA3, VADDR[9]);
  not not_14 (nA4, VADDR[10]);
  nand nand_1 (nand_1_out, nB0, VADDR[1], VADDR[2], VADDR[3], nB4, VADDR[5], nB6, VADDR[7]);
  nand nand_2 (nand_2_out, nB0, nB1, VADDR[2], VADDR[3], VADDR[4], VADDR[5], nB6, VADDR[7]);
  nand nand_3 (LE, nB0, nB1, nB2, nB3, VADDR[4], nB5, VADDR[6], VADDR[7]);
  nand nand_4 (nand_4_out, nB0, nB1, nB2, nB3, nB4, VADDR[5], nB6, VADDR[7]);
  and and_1 (and_1_out, VADDR[11], VADDR[14], VADDR[13], VADDR[12]);
  nand nand_5 (nand_5_out, and_1_out, A0, nA1, nA2, nA3, nA4);
  nand nand_6 (nand_6_out, and_1_out, nA0, nA1, VADDR[8], nA3, nA4);
  nand nand_7 (nVR, and_1_out, A0, nA1, VADDR[8], VADDR[9], VADDR[10]);
  nand nand_8 (nand_8_out, and_1_out, nA0, nA1, nA2, nA3, nA4);
  RS_FF_AS rs_ff_as_1 (.S(~nand_1_out), .R(~nand_2_out), .nQ(HSYNC));  // open: Q
  RS_FF_AS rs_ff_as_2 (.S(~LE), .R(~nand_4_out), .Q(nOE_H));  // open: nQ
  nand nand_9 (nVOE, nOE_V, nOE_H);
  RS_FF_AS rs_ff_as_3 (.S(~nand_5_out), .R(~nand_6_out), .nQ(VSYNC));  // open: Q
  RS_FF_AS rs_ff_as_4 (.S(~nVR), .R(~nand_8_out), .Q(nOE_V));  // open: nQ

  assign B = VDATA[4:0];
  assign G = VDATA[9:5];
  assign R = VDATA[14:10];

  // Other names for the same wires on the sheet: A2 = VADDR[8]; A3 = VADDR[9]; A4 = VADDR[10]; A5 = VADDR[11];
  //   A6 = VADDR[12]; A7 = VADDR[13]; A8 = VADDR[14]; B0 = VADDR[0]; B1 = VADDR[1]; B2 = VADDR[2]; B3 = VADDR[3];
  //   B4 = VADDR[4]; B5 = VADDR[5]; B6 = VADDR[6]; B7 = VADDR[7]
endmodule
