// Digital circuit gputest.dig as structural Verilog
module gputest (
  input  clk
);

  wire gpu_1_hsync, gpu_1_nvoe, gpu_1_vsync, not_1_out;
  wire [4:0] gpu_1_b, gpu_1_g, gpu_1_r;
  wire [14:0] gpu_1_vaddr;
  wire [15:0] rom_1_d;

  ROM #(.AddrBits(15), .Bits(16)) rom_1 (.A(gpu_1_vaddr), .sel(not_1_out), .D(rom_1_d));
  not not_1 (not_1_out, gpu_1_nvoe);
  gpu gpu_1 (
    .VDATA(rom_1_d), .PC(clk), .R(gpu_1_r), .G(gpu_1_g), .B(gpu_1_b), .HSYNC(gpu_1_hsync), .nVOE(gpu_1_nvoe),
    .VSYNC(gpu_1_vsync), .VADDR(gpu_1_vaddr));
  VGA vga_1 (.R(gpu_1_r), .G(gpu_1_g), .B(gpu_1_b), .H(gpu_1_hsync), .V(gpu_1_vsync), .C(clk));

  // Notes on the sheet:
  //   clk: Hz: 36000000
endmodule
