// Digital circuit main.dig as structural Verilog
module main (
  input  in_1
);

  wire _74173_1_pin11, and_1_out, and_2_out, and_3_out, and_4_out, comparator_1_eq, ctrl_1_hlt, ctrl_1_iric,
       ctrl_1_jnz, ctrl_1_nmcr, ctrl_1_npcl, ctrl_1_pce, FLG_CARRY, FLG_SIGN, FLG_ZERO, gpu_1_hsync,
       gpu_1_vsync, memory_controller_1_re_db, memory_controller_1_s0_db, memory_controller_1_s1_db,
       memory_controller_1_we_db, MSL, nand_1_out, nIN_ALA, nIN_ALB, nMAL, nMR, nMW, nOE_reg, not_1_out,
       not_2_out, not_3_out, notconnected_2_out, nOUT_ALU, nPCL, nPCO, nWE_reg, or_1_out, or_2_out, PCE, SWP,
       SWP__STATE, VR;
  wire [2:0] SEL_reg;
  wire [3:0] ALF, gpu_1_b, gpu_1_g, gpu_1_r, prgm_counter_1_dout, rom_1_d;
  wire [5:4] rom_1_d_2;
  wire [11:0] prgm_counter_1_dout_2;
  wire [14:0] memory_controller_1_db__addr, VADDR;
  wire [15:0] VDATA;

  ROM #(.AddrBits(4), .Bits(6)) rom_1 (.A(ALF), .sel(1'b1), .D({rom_1_d_2, rom_1_d}));
  prgm_counter prgm_counter_1 (
    .DIN({prgm_counter_1_dout_2, prgm_counter_1_dout}), .nPCL(nPCL), .CLK(in_1), .PCE(PCE), .nPCO(nPCO),
    .DOUT({prgm_counter_1_dout_2, prgm_counter_1_dout}));
  alu16 alu16_1 (
    .A({prgm_counter_1_dout_2, prgm_counter_1_dout}), .nINA(nIN_ALA),
    .B({prgm_counter_1_dout_2, prgm_counter_1_dout}), .nINB(nIN_ALB), .S(rom_1_d), .M(rom_1_d_2[4]),
    .nCn(rom_1_d_2[5]), .CLK(in_1), .nALUOUT(nOUT_ALU), .O({prgm_counter_1_dout_2, prgm_counter_1_dout}),
    .Cout(FLG_CARRY));
  and and_1 (and_1_out, SEL_reg[0], SEL_reg[1]);
  not not_1 (not_1_out, SEL_reg[2]);
  or or_1 (or_1_out, and_1_out, not_1_out);
  nand nand_1 (nand_1_out, and_1_out, SEL_reg[2]);
  or or_2 (or_2_out, nOE_reg, nand_1_out);
  Comparator #(.Bits(16)) comparator_1 (
    .a({16{1'b0}}), .b({prgm_counter_1_dout_2, prgm_counter_1_dout}), .eq(comparator_1_eq));  // open: gt, lt
  and and_2 (and_2_out, not_2_out, in_1);
  not not_2 (not_2_out, nOUT_ALU);
  reg4x16 reg4x16_0 (
    .DIN({prgm_counter_1_dout_2, prgm_counter_1_dout}), .ADDR(SEL_reg[1:0]), .nOE(nOE_reg), .nWE(nWE_reg),
    .nSEL(SEL_reg[2]), .DOUT({prgm_counter_1_dout_2, prgm_counter_1_dout}));
  reg4x16 reg4x16_1 (
    .DIN({prgm_counter_1_dout_2, prgm_counter_1_dout}), .ADDR(SEL_reg[1:0]), .nOE(nOE_reg), .nWE(nWE_reg),
    .nSEL(or_1_out), .DOUT({prgm_counter_1_dout_2, prgm_counter_1_dout}));
  // NotConnected on prgm_counter_1_dout_2
  _74173 _74173_1 (
    .pin1(or_2_out), .pin2(or_2_out), .pin3(prgm_counter_1_dout[0]), .pin4(prgm_counter_1_dout[1]),
    .pin5(prgm_counter_1_dout[2]), .pin6(prgm_counter_1_dout[3]), .pin7(in_1), .pin8(1'b0), .pin9(1'b0),
    .pin10(1'b0), .pin11(_74173_1_pin11), .pin12(FLG_ZERO), .pin13(FLG_CARRY), .pin14(FLG_SIGN),
    .pin15(1'b0), .pin16(1'b1));
  D_FF d_ff_1 (.D(comparator_1_eq), .C(and_2_out), .Q(FLG_ZERO));  // open: nQ
  D_FF_AS d_ff_as_1 (
    .Set(notconnected_2_out), .D(prgm_counter_1_dout_2[11]), .C(~and_2_out), .Clr(1'b0), .Q(FLG_SIGN));  // open: nQ
  // NotConnected on notconnected_2_out
  // NotConnected on _74173_1_pin11
  // Probe BUS on {prgm_counter_1_dout_2, prgm_counter_1_dout}
  JK_FF jk_ff_1 (.J(SWP), .C(in_1), .K(SWP), .Q(SWP__STATE));  // open: nQ
  ctrl ctrl_1 (
    .IRI(ctrl_1_iric), .IRDI({prgm_counter_1_dout_2, prgm_counter_1_dout}), .CLK(in_1), .nMCRI(ctrl_1_nmcr),
    .nMW(nMW), .nMR(nMR), .MSL(MSL), .nMAL(nMAL), .IRIC(ctrl_1_iric), .RSEL(SEL_reg), .nRGI(nWE_reg),
    .nRGO(nOE_reg), .nIN_ALA(nIN_ALA), .nIN_ALB(nIN_ALB), .ALF(ALF), .nALO(nOUT_ALU), .PCE(ctrl_1_pce),
    .nPCL(ctrl_1_npcl), .nPCO(nPCO), .HLT(ctrl_1_hlt), .nMCR(ctrl_1_nmcr), .SWP(SWP), .JNZ(ctrl_1_jnz));
  gpu gpu_1 (
    .PC(in_1), .VDATA(VDATA), .R(gpu_1_r), .G(gpu_1_g), .B(gpu_1_b), .HSYNC(gpu_1_hsync),
    .VSYNC(gpu_1_vsync), .VADDR(VADDR), .nVOE(VR));
  memory_controller memory_controller_1 (
    .nMAL(nMAL), .CLK(in_1), .BUS({prgm_counter_1_dout_2, prgm_counter_1_dout}), .CRE(nMR), .CWE(nMW),
    .DBS(SWP__STATE), .RSE(MSL), .S0_DB(memory_controller_1_s0_db), .DB__ADDR(memory_controller_1_db__addr),
    .WE_DB(memory_controller_1_we_db), .RE_DB(memory_controller_1_re_db), .S1_DB(memory_controller_1_s1_db));
  not not_3 (not_3_out, ctrl_1_nmcr);
  VGA vga_1 (.R(gpu_1_r), .G(gpu_1_g), .B(gpu_1_b), .H(gpu_1_hsync), .V(gpu_1_vsync), .C(in_1));
  LED led_1 (.in(ctrl_1_hlt));
  LED led_2 (.in(not_3_out));
  and and_3 (and_3_out, FLG_ZERO, ctrl_1_jnz);
  // Probe on VDATA
  double_buffer_el double_buffer_el_1 (
    .SEL(memory_controller_1_s0_db), .ADDR0(memory_controller_1_db__addr), .W0(memory_controller_1_we_db),
    .R0(memory_controller_1_re_db), .ADDR1(VADDR), .W1(1'b1), .R1(VR),
    .DATA0({prgm_counter_1_dout_2, prgm_counter_1_dout}), .DATA1(VDATA));
  double_buffer_el double_buffer_el_2 (
    .SEL(memory_controller_1_s1_db), .ADDR0(memory_controller_1_db__addr), .W0(memory_controller_1_we_db),
    .R0(memory_controller_1_re_db), .ADDR1(VADDR), .W1(1'b1), .R1(VR),
    .DATA0({prgm_counter_1_dout_2, prgm_counter_1_dout}), .DATA1(VDATA));
  Multiplexer multiplexer_1 (.sel(ctrl_1_jnz), .in_0(ctrl_1_npcl), .in_1(and_3_out), .out(nPCL));
  and and_4 (and_4_out, ctrl_1_jnz, nPCL);
  Multiplexer multiplexer_2 (.sel(ctrl_1_jnz), .in_0(ctrl_1_pce), .in_1(and_4_out), .out(PCE));

  // Other names for the same wires on the sheet: CLK = in_1

  // Notes on the sheet:
  //   contents of rom_1 (hex, n*v repeats v):
  //   33,30,29,23,36,3e,31,34,0,2f,2c,14,6,3c,3b
  //   0b111: FLAGS
  //   FLAGS REGISTER
  //   contents of PROGRAM (hex, n*v repeats v):
  //   C:\Users\Aryam\OneDrive\Documents\AOS16\assembler\cmake-build-debug\test.o true
endmodule
