// Digital circuit memory_controller.dig as structural Verilog
module memory_controller (
  input  nMAL,
  input  CLK,
  input  [15:0] BUS,
  input  CRE,
  input  CWE,
  input  DBS,
  input  RSE,
  output S0_DB,
  output [14:0] DB__ADDR,
  output WE_DB,
  output RE_DB,
  output S1_DB
);

  wire ADDR15, not_2_out, not_3_out, not_4_out, nRE_RAM, nRE_ROM, nWE_RAM;

  not not_1 (S1_DB, DBS);
  or or_1 (nWE_RAM, ADDR15, RSE, CWE);
  or or_2 (nRE_RAM, ADDR15, RSE, CRE);
  not not_2 (not_2_out, RSE);
  or or_3 (nRE_ROM, not_2_out, CRE);
  reg16 reg16_1 (.nWE(nMAL), .CLK(CLK), .DIN(BUS), .nOE(1'b0), .DOUT({ADDR15, DB__ADDR}));
  not not_3 (not_3_out, nRE_ROM);
  not not_4 (not_4_out, ADDR15);
  ROM #(.AddrBits(16), .Bits(16)) PROGRAM (.A({ADDR15, DB__ADDR}), .sel(not_3_out), .D(BUS));
  ramchip ramchip_1 (.nWE(nWE_RAM), .D(BUS), .nOE(nRE_RAM), .ADDR(DB__ADDR));
  or or_4 (RE_DB, CRE, RSE, not_4_out);
  or or_5 (WE_DB, not_4_out, RSE, CWE);

  assign S0_DB = DBS;

  // Notes on the sheet:
  //   contents of PROGRAM (hex, n*v repeats v):
  //   1a20,0,1aa0,0,1ae0,8000,f8,1a60,0,1a93,a0,1,60,1,e0,100,1860,40
  //   ,2400,9,20,1,1820,40,2400,4,2000,2200,1b
endmodule
