// Digital circuit prgm_counter.dig as structural Verilog
module prgm_counter (
  input  [15:0] DIN,
  input  nPCL,
  input  CLK,
  input  PCE,
  input  nPCO,
  output [15:0] DOUT
);

  wire [15:0] counterpreset_1_out;

  CounterPreset #(.Bits(16)) counterpreset_1 (
    .en(PCE), .C(CLK), .dir(1'b0), .in(DIN), .ld(~nPCL), .clr(1'b0), .out(counterpreset_1_out));  // open: ovf
  assign DOUT = ~nPCO ? counterpreset_1_out : 16'bz;  // DriverInvSel driverinvsel_1
endmodule
