// Digital circuit reg16.dig as structural Verilog
module reg16 (
  input  nWE,
  input  CLK,
  input  [15:0] DIN,
  input  nOE,
  output [15:0] DOUT
);

  wire [15:0] register_1_q;

  Register #(.Bits(16)) register_1 (.D(DIN), .C(CLK), .en(~nWE), .Q(register_1_q));
  assign DOUT = ~nOE ? register_1_q : 16'bz;  // DriverInvSel driverinvsel_1
endmodule
