// Digital circuit reg4x16.dig as structural Verilog
module reg4x16 (
  input  [15:0] DIN,
  input  [1:0] ADDR,
  input  nOE,
  input  nWE,
  input  nSEL,
  output [15:0] DOUT
);

  wire or_1_out, or_2_out;

  or or_1 (or_1_out, nSEL, nOE);
  or or_2 (or_2_out, nSEL, nWE);
  _74ls670 _74ls670_1 (.DIN(DIN[3:0]), .ADDR(ADDR), .nWE(or_2_out), .nOE(or_1_out), .DOUT(DOUT[3:0]));
  _74ls670 _74ls670_2 (.DIN(DIN[7:4]), .ADDR(ADDR), .nWE(or_2_out), .nOE(or_1_out), .DOUT(DOUT[7:4]));
  _74ls670 _74ls670_3 (.DIN(DIN[11:8]), .ADDR(ADDR), .nWE(or_2_out), .nOE(or_1_out), .DOUT(DOUT[11:8]));
  _74ls670 _74ls670_4 (.DIN(DIN[15:12]), .ADDR(ADDR), .nWE(or_2_out), .nOE(or_1_out), .DOUT(DOUT[15:12]));
endmodule
