// Digital circuit registers.dig as structural Verilog
module registers (
  input  [3:0] DIN,
  input  [2:0] SEL,
  input  nOE,
  input  nWE
);

  wire and_1_out, not_1_out, or_1_out, reg4x16_1_p5, undriven;
  wire [1:0] reg4x16_1_p2;

  not not_1 (not_1_out, reg4x16_1_p5);
  and and_1 (and_1_out, reg4x16_1_p2[0], undriven);
  or or_1 (or_1_out, and_1_out, not_1_out);
  // reg4x16 reg4x16_1: pin names not known; wires that end beside it: DIN, reg4x16_1_p2, nOE, nWE, reg4x16_1_p5
  // reg4x16 reg4x16_2: pin names not known; wires that end beside it: DIN, reg4x16_1_p2, nOE, nWE, or_1_out
  // Pins of 1 and 2 bits meet at reg4x16_1_p2
endmodule
